// Logisim project Jogo Digital Heist_V2.circ as structural Verilog: 2 circuits, main circuit main
module main (
  input  CLOCK,
  input  BUG,
  input  WALL_A,
  input  WALL_B,
  input  WALL_C,
  input  SEARCH,
  input  WALL_D,
  input  DATA,
  input  EMP,
  input  KEY_1,
  input  KEY_2,
  input  KEY_3,
  input  KEY_4,
  input  KEY_5,
  input  KEY_6
);

  wire and_1_out, and_2_out, and_3_out, and_4_out, buffer_1_out, d_ff_1_q, d_ff_2_q, d_ff_3_q, d_ff_4_q,
       decoder_1_out0, decoder_1_out1, decoder_1_out2, decoder_1_out3, firewall_1_out_5, firewall_1_out_6,
       firewall_1_out_7, firewall_1_out_8, firewall_1_out_9, firewall_1_out_10, firewall_1_out_11,
       firewall_1_out_12;
  wire [1:0] multiplexer_2_out;
  wire [3:0] counter_1_q, counter_2_q, counter_3_q, counter_4_q, counter_5_q;

  Hex_Digit_Display hex_digit_display_1 (.value({WALL_D, WALL_C, WALL_B, WALL_A}));  // open: dp
  Hex_Digit_Display hex_digit_display_2 (.value({1'b0, KEY_1, KEY_2, KEY_3}));  // open: dp
  Hex_Digit_Display hex_digit_display_3 (.value({1'b0, KEY_4, KEY_5, KEY_6}));  // open: dp
  Firewall firewall_1 (
    .A(WALL_A), .B(WALL_B), .C(WALL_C), .D(WALL_D), .out_5(firewall_1_out_5), .out_6(firewall_1_out_6),
    .out_7(firewall_1_out_7), .out_8(firewall_1_out_8), .out_9(firewall_1_out_9), .out_10(firewall_1_out_10),
    .out_11(firewall_1_out_11), .out_12(firewall_1_out_12));
  D_Flip_Flop d_ff_1 (.clk(CLOCK), .D(DATA), .Q(d_ff_1_q), .preset(SEARCH), .reset(EMP));  // open: Qn, en
  Multiplexer #(.select(3)) multiplexer_1 (
    .in0(firewall_1_out_5), .in1(firewall_1_out_6), .in2(firewall_1_out_7), .in3(firewall_1_out_8),
    .in4(firewall_1_out_9), .in5(firewall_1_out_10), .in6(firewall_1_out_11), .in7(firewall_1_out_12),
    .out(multiplexer_2_out[1]), .sel({KEY_1, KEY_2, KEY_3}), .en(1'b1));
  D_Flip_Flop d_ff_2 (.clk(CLOCK), .D(d_ff_1_q), .Q(d_ff_2_q), .preset(SEARCH), .reset(EMP));  // open: Qn, en
  D_Flip_Flop d_ff_3 (.clk(CLOCK), .D(d_ff_2_q), .Q(d_ff_3_q), .preset(SEARCH), .reset(EMP));  // open: Qn, en
  Multiplexer #(.select(3)) multiplexer_2 (
    .in0(firewall_1_out_5), .in1(firewall_1_out_6), .in2(firewall_1_out_7), .in3(firewall_1_out_8),
    .in4(firewall_1_out_9), .in5(firewall_1_out_10), .in6(firewall_1_out_11), .in7(firewall_1_out_12),
    .out(multiplexer_2_out[0]), .sel({KEY_4, KEY_5, KEY_6}), .en(1'b1));
  Decoder #(.select(2)) decoder_1 (
    .out0(decoder_1_out0), .out1(decoder_1_out1), .out2(decoder_1_out2), .out3(decoder_1_out3),
    .sel(multiplexer_2_out), .en(d_ff_4_q));
  D_Flip_Flop d_ff_4 (.clk(CLOCK), .D(d_ff_3_q), .Q(d_ff_4_q), .preset(SEARCH), .reset(EMP));  // open: Qn, en
  buf buffer_1 (buffer_1_out, d_ff_4_q);
  and and_1 (and_1_out, decoder_1_out0, CLOCK);
  and and_2 (and_2_out, decoder_1_out1, CLOCK);
  and and_3 (and_3_out, decoder_1_out2, CLOCK);
  and and_4 (and_4_out, decoder_1_out3, CLOCK);
  Counter #(.width(4), .max('hf)) counter_1 (
    .load(buffer_1_out), .Q(counter_1_q), .clk(CLOCK), .clr(buffer_1_out));  // open: D, count, carry
  Hex_Digit_Display hex_digit_display_4 (.value(counter_2_q));  // open: dp
  Counter #(.width(4), .max('hf)) counter_2 (
    .load(BUG), .Q(counter_2_q), .clk(and_1_out));  // open: D, count, carry, clr
  Hex_Digit_Display hex_digit_display_5 (.value(counter_3_q));  // open: dp
  Counter #(.width(4), .max('hf)) counter_3 (
    .load(BUG), .Q(counter_3_q), .clk(and_2_out));  // open: D, count, carry, clr
  Hex_Digit_Display hex_digit_display_6 (.value(counter_4_q));  // open: dp
  Counter #(.width(4), .max('hf)) counter_4 (
    .load(BUG), .Q(counter_4_q), .clk(and_3_out));  // open: D, count, carry, clr
  Hex_Digit_Display hex_digit_display_7 (.value(counter_5_q));  // open: dp
  Counter #(.width(4), .max('hf)) counter_5 (
    .load(BUG), .Q(counter_5_q), .clk(and_4_out));  // open: D, count, carry, clr
  Hex_Digit_Display hex_digit_display_8 (.value(counter_1_q));  // open: dp

  // Notes on the sheet:
  //   BITS DE
  //   DADOS
  //   BITS DE
  //   ENDEREÇAMENTO
  //   BITS DE
  //   ENDEREÇAMENTO
  //   DATABASE
  //   MAINFRAME
  //   MAINFRAME
  //   CATADORES
  //   ELITE
  //   CORTE
  //   INTERNOS
  //   ZEROS
endmodule

module Firewall (
  input  A,
  input  B,
  input  C,
  input  D,
  output out_5,
  output out_6,
  output out_7,
  output out_8,
  output out_9,
  output out_10,
  output out_11,
  output out_12
);

  and and_1 (out_5, A, B);
  or or_1 (out_6, C, D);
  nand nand_1 (out_7, A, C);
  nor nor_1 (out_8, B, D);
  nor nor_2 (out_9, A, D);
  xor xor_1 (out_10, B, C);
  xnor xnor_1 (out_11, A, B);
  not not_1 (out_12, D);
endmodule
